// Digital circuit 2chooser64.dig as structural Verilog
module _2chooser64 (
  input  a0,
  input  a1,
  input  a2,
  input  a3,
  input  a4,
  input  a5,
  input  b0,
  input  b1,
  input  b2,
  input  b3,
  input  b4,
  input  b5,
  input  c,
  output z0,
  output z1,
  output z2,
  output z3,
  output z4,
  output z5
);

  Multiplexer multiplexer_1 (.sel(c), .in_0(a0), .in_1(b0), .out(z0));
  Multiplexer multiplexer_2 (.sel(c), .in_0(a1), .in_1(b1), .out(z1));
  Multiplexer multiplexer_3 (.sel(c), .in_0(a2), .in_1(b2), .out(z2));
  Multiplexer multiplexer_4 (.sel(c), .in_0(a3), .in_1(b3), .out(z3));
  Multiplexer multiplexer_5 (.sel(c), .in_0(a4), .in_1(b4), .out(z4));
  Multiplexer multiplexer_6 (.sel(c), .in_0(a5), .in_1(b5), .out(z5));
endmodule
