// Digital circuit comparador64.dig as structural Verilog
module comparador64 (
  input  a0,
  input  a1,
  input  a2,
  input  a3,
  input  a4,
  input  a5,
  input  b0,
  input  b1,
  input  b2,
  input  b3,
  input  b4,
  input  b5,
  output a,
  output b,
  output e
);

  wire and_1_out, and_2_out, and_3_out, and_4_out, and_5_out, and_6_out, and_7_out, and_8_out, and_9_out,
       comparator_1_eq, comparator_1_lt, comparator_2_eq, comparator_2_lt, comparator_3_eq, comparator_3_lt,
       comparator_4_eq, comparator_4_lt, comparator_5_eq, comparator_5_lt, comparator_6_eq, comparator_6_lt,
       or_2_out, or_3_out, or_4_out, or_5_out, or_6_out;

  Comparator comparator_1 (.a(b0), .b(a0), .eq(comparator_1_eq), .lt(comparator_1_lt));  // open: gt
  or or_1 (a, or_2_out, comparator_1_lt);
  Comparator comparator_2 (.a(b1), .b(a1), .eq(comparator_2_eq), .lt(comparator_2_lt));  // open: gt
  and and_1 (and_1_out, comparator_2_lt, comparator_1_eq);
  or or_2 (or_2_out, or_3_out, and_1_out);
  Comparator comparator_3 (.a(b2), .b(a2), .eq(comparator_3_eq), .lt(comparator_3_lt));  // open: gt
  and and_2 (and_2_out, and_6_out, comparator_3_lt);
  or or_3 (or_3_out, or_4_out, and_2_out);
  Comparator comparator_4 (.a(b3), .b(a3), .eq(comparator_4_eq), .lt(comparator_4_lt));  // open: gt
  and and_3 (and_3_out, and_7_out, comparator_4_lt);
  or or_4 (or_4_out, or_5_out, and_3_out);
  Comparator comparator_5 (.a(b4), .b(a4), .eq(comparator_5_eq), .lt(comparator_5_lt));  // open: gt
  Comparator comparator_6 (.a(b5), .b(a5), .eq(comparator_6_eq), .lt(comparator_6_lt));  // open: gt
  and and_4 (and_4_out, and_9_out, comparator_6_lt);
  and and_5 (and_5_out, and_8_out, comparator_5_lt);
  or or_5 (or_5_out, and_4_out, and_5_out);
  and and_6 (and_6_out, comparator_1_eq, comparator_2_eq);
  and and_7 (and_7_out, and_6_out, comparator_3_eq);
  and and_8 (and_8_out, and_7_out, comparator_4_eq);
  and and_9 (and_9_out, and_8_out, comparator_5_eq);
  and and_10 (e, and_9_out, comparator_6_eq);
  or or_6 (or_6_out, e, a);
  not not_1 (b, or_6_out);
endmodule
